# Fritzing sketch buttons control (saved by Fritzing 0.9.3b)
breadboards: 1

parts:
  S1 = Pushbutton [package="[THT]"]
  S2 = Pushbutton [package="[THT]"]
  S3 = Pushbutton [package="[THT]"]
  R1 = Resistor [tolerance=±5% resistance=220 package=THT]
  R2 = Resistor [tolerance=±5% resistance=220 package=THT]
  R3 = Resistor [tolerance=±5% resistance=220 package=THT]
  J1 = female pin header, 3 pins [form="♀ (female)"]
  J2 = female pin header, 2 pins [form="♀ (female)"]

nets:
  N1: S1.Pin_1, S1.Pin_2, R1.Pin_1, J1.pin1
  N2: S1.Pin_3, S1.Pin_4, S2.Pin_3, S2.Pin_4, S3.Pin_3, S3.Pin_4, J2.pin2
  N3: S2.Pin_1, S2.Pin_2, R2.Pin_1, J1.pin2
  N4: S3.Pin_1, S3.Pin_2, R3.Pin_1, J1.pin3
  N5: R1.Pin_0, R2.Pin_0, R3.Pin_0, J2.pin1
