# Fritzing sketch extruder control 2 (saved by Fritzing 0.9.3b)
circuit board: 8.46667cm x 5.64444cm
breadboards: 1

parts:
  J11 = Screw terminal - 2 pins [package=THT]
  F2 = FUSE [package=fuse_5mm]
  U3 = mystery part, 3 pins [chip_label=LM7812]
  U4 = mystery part, 3 pins [chip_label=LM7805]
  C27 = Tantalum Capacitor [capacitance=47µF package="B 3528 [SMD, tantalum]"]
  C28 = Tantalum Capacitor [capacitance=47µF package="B 3528 [SMD, tantalum]"]
  C29 = Tantalum Capacitor [capacitance=47µF package="B 3528 [SMD, tantalum]"]
  C30 = Tantalum Capacitor [capacitance=10µF package="B 3528 [SMD, tantalum]"]
  C31 = Tantalum Capacitor [capacitance=10µF package="B 3528 [SMD, tantalum]"]
  C32 = Ceramic Capacitor [capacitance=1µF package="0805 [SMD, multilayer]"]
  C33 = Ceramic Capacitor [capacitance=0.1µF package="0805 [SMD, multilayer]"]
  C34 = Ceramic Capacitor [capacitance=0.1µF package="0805 [SMD, multilayer]"]
  C35 = Ceramic Capacitor [capacitance=0.1µF package="0805 [SMD, multilayer]"]
  Q2 = Basic FET P-Channel [package="TO220 [THT]"]
  LED2 = smd LED [color="Red (633nm)" package="0805 [SMD]"]
  R6 = Resistor [tolerance=±5% resistance=1.8k package="0805 [SMD]"]
  J12 = Screw terminal - 2 pins [package=THT]
  R5 = Resistor [tolerance=±5% resistance=100k package="0805 [SMD]"]
  R4 = Resistor [tolerance=±5% resistance=10 package="0805 [SMD]"]

nets:
  GND: J11.pin1, U3.pin2, U4.pin2, C27.-, C28.-, C29.-, C30.-, C31.-, C32.0, C33.0, C34.0, C35.0, Q2.source, R5.Pin_1
  N1: J11.pin2, F2.1
  24V: F2.2, U4.pin1, C27.+, C29.+, C32.1, C33.1, R6.Pin_1, J12.pin2
  N2: U3.pin1, C28.+
  12V: U3.pin3, C31.+, C34.1
  N3: U4.pin3, C35.1
  5V: C30.+
  N4: Q2.gate, R4.Pin_1
  N5: Q2.drain, LED2.cathode, J12.pin1
  N6: LED2.anode, R6.Pin_0
  heater 1_1: R5.Pin_0, R4.Pin_0
