# Fritzing sketch extruder control 3 (saved by Fritzing 0.9.3b)
circuit board: 10.1776cm x 5.36194cm
breadboards: 1

parts:
  J13 = screw terminal, 8 pins
  J1 = screw terminal, 7 pins
  J14 = screw terminal, 4 pins
  J11 = Screw terminal - 2 pins [package=THT]
  U5 = mystery part, 3 pins [chip_label=LM7805]
  J18 = male pin header, 3 pins [form="♂ (male)"]
  J19 = male pin header, 3 pins [form="♂ (male)"]
  J20 = male pin header, 3 pins [form="♂ (male)"]
  J21 = male pin header, 3 pins [form="♂ (male)"]
  J22 = male pin header, 3 pins [form="♂ (male)"]
  C45 = Tantalum Capacitor [capacitance=47µF voltage=20 part_number=T491D476K025AT package="D 7343 [SMD, tantalum]"]
  C46 = Tantalum Capacitor [capacitance=10µF part_number=T491A106M016AT package="A 3216 [SMD, tantalum]"]
  C47 = Ceramic Capacitor [capacitance=0.1µF voltage=35V part_number=C0603C104K4RACTU package="0603 [SMD, multilayer]"]
  C17 = Ceramic Capacitor [capacitance=0.01µF part_number=C0603C103K4RACTU package="0603 [SMD, multilayer]"]
  C23 = Ceramic Capacitor [capacitance=0.01µF part_number=C0603C103K4RACTU package="0603 [SMD, multilayer]"]
  C20 = Ceramic Capacitor [capacitance=1µF part_number=C0603C105K4RACTU package="0603 [SMD, multilayer]"]
  C26 = Ceramic Capacitor [capacitance=0.1µF part_number=C0603C104K4RACTU package="0603 [SMD, multilayer]"]
  C29 = Tantalum Capacitor [capacitance=10µF part_number=C0603C104K4RACTU package="A 3216 [SMD, tantalum]"]
  R29 = Resistor [tolerance=±5% resistance=100 part_number=RC0603FR-07100RL package="0603 [SMD]"]
  R32 = Resistor [tolerance=±5% resistance=100 part_number=RC0603FR-07100RL package="0603 [SMD]"]
  R35 = Resistor [tolerance=±5% resistance=1M part_number=RC0603FR-071ML package="0603 [SMD]"]
  C48 = Ceramic Capacitor [capacitance=0.01µF part_number=C0603C103K4RACTU package="0603 [SMD, multilayer]"]
  C49 = Ceramic Capacitor [capacitance=1µF part_number=C0603C105K4RACTU package="0603 [SMD, multilayer]"]
  C50 = Ceramic Capacitor [capacitance=0.01µF part_number=C0603C103K4RACTU package="0603 [SMD, multilayer]"]
  R36 = Resistor [tolerance=±5% resistance=100 part_number=RC0603FR-07100RL package="0603 [SMD]"]
  R37 = Resistor [tolerance=±5% resistance=100 part_number=RC0603FR-07100RL package="0603 [SMD]"]
  R38 = Resistor [tolerance=±5% resistance=1M part_number=RC0603FR-071ML package="0603 [SMD]"]
  J23 = Screw terminal - 2 pins [package=THT]
  C51 = Ceramic Capacitor [capacitance=0.1µF part_number=C0603C104K4RACTU package="0603 [SMD, multilayer]"]
  C52 = Tantalum Capacitor [capacitance=10µF part_number=C0603C104K4RACTU package="A 3216 [SMD, tantalum]"]
  C53 = Ceramic Capacitor [capacitance=0.01µF part_number=C0603C103K4RACTU package="0603 [SMD, multilayer]"]
  C54 = Ceramic Capacitor [capacitance=0.01µF part_number=C0603C103K4RACTU package="0603 [SMD, multilayer]"]
  C55 = Ceramic Capacitor [capacitance=1µF part_number=C0603C105K4RACTU package="0603 [SMD, multilayer]"]
  C56 = Ceramic Capacitor [capacitance=1µF part_number=C0603C105K4RACTU package="0603 [SMD, multilayer]"]
  C57 = Ceramic Capacitor [capacitance=0.01µF part_number=C0603C103K4RACTU package="0603 [SMD, multilayer]"]
  C58 = Ceramic Capacitor [capacitance=0.01µF part_number=C0603C103K4RACTU package="0603 [SMD, multilayer]"]
  R39 = Resistor [tolerance=±5% resistance=100 part_number=RC0603FR-07100RL package="0603 [SMD]"]
  R40 = Resistor [tolerance=±5% resistance=100 part_number=RC0603FR-07100RL package="0603 [SMD]"]
  R41 = Resistor [tolerance=±5% resistance=100 part_number=RC0603FR-07100RL package="0603 [SMD]"]
  R42 = Resistor [tolerance=±5% resistance=100 part_number=RC0603FR-07100RL package="0603 [SMD]"]
  R43 = Resistor [tolerance=±5% resistance=1M part_number=RC0603FR-071ML package="0603 [SMD]"]
  R44 = Resistor [tolerance=±5% resistance=1M part_number=RC0603FR-071ML package="0603 [SMD]"]
  J24 = Screw terminal - 2 pins [package=THT]
  J25 = Screw terminal - 2 pins [package=THT]
  C59 = Ceramic Capacitor [capacitance=0.1µF part_number=C0603C104K4RACTU package="0603 [SMD, multilayer]"]
  C60 = Ceramic Capacitor [capacitance=0.1µF part_number=C0603C104K4RACTU package="0603 [SMD, multilayer]"]
  C61 = Tantalum Capacitor [capacitance=10µF part_number=C0603C104K4RACTU package="A 3216 [SMD, tantalum]"]
  C62 = Tantalum Capacitor [capacitance=10µF part_number=C0603C104K4RACTU package="A 3216 [SMD, tantalum]"]
  C63 = Ceramic Capacitor [capacitance=0.01µF part_number=C0603C103K4RACTU package="0603 [SMD, multilayer]"]
  C64 = Ceramic Capacitor [capacitance=1µF part_number=C0603C105K4RACTU package="0603 [SMD, multilayer]"]
  C65 = Ceramic Capacitor [capacitance=0.01µF part_number=C0603C103K4RACTU package="0603 [SMD, multilayer]"]
  R45 = Resistor [tolerance=±5% resistance=100 part_number=RC0603FR-07100RL package="0603 [SMD]"]
  R46 = Resistor [tolerance=±5% resistance=100 part_number=RC0603FR-07100RL package="0603 [SMD]"]
  R47 = Resistor [tolerance=±5% resistance=1M part_number=RC0603FR-071ML package="0603 [SMD]"]
  J26 = Screw terminal - 2 pins [package=THT]
  C66 = Ceramic Capacitor [capacitance=0.1µF part_number=C0603C104K4RACTU package="0603 [SMD, multilayer]"]
  C67 = Tantalum Capacitor [capacitance=10µF part_number=C0603C104K4RACTU package="A 3216 [SMD, tantalum]"]
  IC9 = SO08 [chip_label=AD8495 part_number=AD8495ARMZ package=SO]
  IC8 = SO08 [chip_label=AD8495 part_number=AD8495ARMZ package=SO]
  IC7 = SO08 [chip_label=AD8495 part_number=AD8495ARMZ package=SO]
  IC6 = SO08 [chip_label=AD8495 part_number=AD8495ARMZ package=SO]
  IC5 = SO08 [chip_label=AD8495 part_number=AD8495ARMZ package=SO]
  J2 = screw terminal, 2 pins
  Part1 = Arduino Mega 2560 (Rev3)

nets:
  ssr1: J13.pin1, Part1.D22
  GND: J13.pin2, J13.pin4, J13.pin6, J13.pin8, J1.pin2, U5.pin2, J18.pin3, J19.pin3, J20.pin3, J21.pin3, J22.pin3, C45.-, C46.-, C47.0, C17.1, C23.0, C48.1, C50.0, C53.1, C54.1, C57.0, C58.0, C63.1, C65.0, J2.pin1, Part1.GND
  ssr2: J13.pin3, Part1.D24
  ssr3: J13.pin5, Part1.D26
  ssr4: J13.pin7, Part1.D28
  5V: J1.pin1, J18.pin2, J19.pin2, J20.pin2, J21.pin2, J22.pin2, C46.+, C26.1, C29.+, C51.1, C52.+, C59.1, C60.1, C61.+, C62.+, C66.1, C67.+, IC9.7, IC8.7, IC7.7, IC6.7, IC5.7, Part1.VIN
  sda: J1.pin3, Part1.D20/SDA
  slc: J1.pin4, Part1.D21/SCL
  enc 1: J1.pin5, Part1.D17_PWM/RX2
  enc 2: J1.pin6, Part1.D18/TX1
  button: J1.pin7, Part1.D19/RX1
  RO: J14.pin1, Part1.D7_PWM
  RE: J14.pin2, Part1.D6_PWM
  DE: J14.pin3, Part1.D5_PWM
  DI: J14.pin4, Part1.D4_PWM
  N1: J11.pin1, R29.Pin_1
  N2: J11.pin2, R32.Pin_1, R35.Pin_1
  N3: U5.pin1, C45.+, J2.pin2
  N4: U5.pin3, C47.1
  pwm sig: J18.pin1, Part1.D9_PWM
  aux 1: J19.pin1, Part1.D11_PWM
  aux 2: J20.pin1, Part1.D12_PWM
  aux 3: J21.pin1, Part1.D13_PWM
  aux: J22.pin1, Part1.D10_PWM
  N5: C17.0, C20.1, R29.Pin_0, IC5.8
  N6: C23.1, C20.0, R32.Pin_0, IC5.1
  N7: C26.0, C29.-, R35.Pin_0, IC5.2, IC5.3
  N8: C48.0, C49.1, R36.Pin_0, IC6.8
  N9: C49.0, C50.1, R37.Pin_0, IC6.1
  N10: R36.Pin_1, J23.pin1
  N11: R37.Pin_1, R38.Pin_1, J23.pin2
  N12: R38.Pin_0, C51.0, C52.-, IC6.2, IC6.3
  N13: C53.0, C55.1, R39.Pin_0, IC7.8
  N14: C54.0, C56.1, R40.Pin_0, IC8.8
  N15: C55.0, C57.1, R41.Pin_0, IC7.1
  N16: C56.0, C58.1, R42.Pin_0, IC8.1
  N17: R39.Pin_1, J24.pin1
  N18: R40.Pin_1, J25.pin1
  N19: R41.Pin_1, R43.Pin_1, J24.pin2
  N20: R42.Pin_1, R44.Pin_1, J25.pin2
  N21: R43.Pin_0, C59.0, C61.-, IC7.2, IC7.3
  N22: R44.Pin_0, C60.0, C62.-, IC8.2, IC8.3
  N23: C63.0, C64.1, R45.Pin_0, IC9.8
  N24: C64.0, C65.1, R46.Pin_0, IC9.1
  N25: R45.Pin_1, J26.pin1
  N26: R46.Pin_1, R47.Pin_1, J26.pin2
  N27: R47.Pin_0, C66.0, C67.-, IC9.2, IC9.3
  TC5: IC9.5, IC9.6, Part1.A4
  TC4: IC8.5, IC8.6, Part1.A3
  TC3: IC7.5, IC7.6, Part1.A2
  TC2: IC6.5, IC6.6, Part1.A1
  TC1: IC5.5, IC5.6, Part1.A0

notes:
  power in
  control pannel
  Relay Out
  thermocouple 1
  VFD Breakout
  Pwm controller
  thermocouple 2
  thermocouple 3
  thermocouple 4
  Open Extruder
  Control Board
  V1.0
