# Fritzing sketch extruder control 4 (saved by Fritzing 0.9.3b)
circuit board: 10.1776cm x 5.36194cm
breadboards: 1

parts:
  J13 = screw terminal, 8 pins
  J1 = screw terminal, 7 pins
  J14 = screw terminal, 4 pins
  J11 = Screw terminal - 2 pins [package=THT]
  U5 = mystery part, 3 pins [chip_label=LM7805]
  J18 = male pin header, 3 pins [form="♂ (male)"]
  J19 = male pin header, 3 pins [form="♂ (male)"]
  J20 = male pin header, 3 pins [form="♂ (male)"]
  J21 = male pin header, 3 pins [form="♂ (male)"]
  J22 = male pin header, 3 pins [form="♂ (male)"]
  C45 = Tantalum Capacitor [capacitance=47µF voltage=20 part_number=T491D476K025AT package="D 7343 [SMD, tantalum]"]
  C46 = Tantalum Capacitor [capacitance=10µF part_number=T491A106M016AT package="A 3216 [SMD, tantalum]"]
  C47 = Ceramic Capacitor [capacitance=0.1µF voltage=35V part_number=C0603C104K4RACTU package="0603 [SMD, multilayer]"]
  C17 = Ceramic Capacitor [capacitance=0.01µF part_number=C0603C103K4RACTU package="0603 [SMD, multilayer]"]
  C23 = Ceramic Capacitor [capacitance=0.01µF part_number=C0603C103K4RACTU package="0603 [SMD, multilayer]"]
  C20 = Ceramic Capacitor [capacitance=1µF part_number=C0603C105K4RACTU package="0603 [SMD, multilayer]"]
  C26 = Ceramic Capacitor [capacitance=0.1µF part_number=C0603C104K4RACTU package="0603 [SMD, multilayer]"]
  C29 = Tantalum Capacitor [capacitance=10µF part_number=C0603C104K4RACTU package="A 3216 [SMD, tantalum]"]
  R32 = Resistor [tolerance=±5% resistance=100 part_number=RC0603FR-07100RL package="0603 [SMD]"]
  R35 = Resistor [tolerance=±5% resistance=1M part_number=RC0603FR-071ML package="0603 [SMD]"]
  J2 = screw terminal, 2 pins
  U6 = AD8495 SMD [package=msop8]
  R29 = Resistor [tolerance=±5% resistance=100 part_number=RC0603FR-07100RL package="0603 [SMD]"]
  U7 = AD8495 SMD [package=msop8]
  C48 = Ceramic Capacitor [capacitance=0.01µF part_number=C0603C103K4RACTU package="0603 [SMD, multilayer]"]
  C49 = Ceramic Capacitor [capacitance=1µF part_number=C0603C105K4RACTU package="0603 [SMD, multilayer]"]
  C50 = Ceramic Capacitor [capacitance=0.01µF part_number=C0603C103K4RACTU package="0603 [SMD, multilayer]"]
  R36 = Resistor [tolerance=±5% resistance=100 part_number=RC0603FR-07100RL package="0603 [SMD]"]
  R37 = Resistor [tolerance=±5% resistance=100 part_number=RC0603FR-07100RL package="0603 [SMD]"]
  R38 = Resistor [tolerance=±5% resistance=1M part_number=RC0603FR-071ML package="0603 [SMD]"]
  J23 = Screw terminal - 2 pins [package=THT]
  C51 = Ceramic Capacitor [capacitance=0.1µF part_number=C0603C104K4RACTU package="0603 [SMD, multilayer]"]
  C52 = Tantalum Capacitor [capacitance=10µF part_number=C0603C104K4RACTU package="A 3216 [SMD, tantalum]"]
  U8 = AD8495 SMD [package=msop8]
  C53 = Ceramic Capacitor [capacitance=0.01µF part_number=C0603C103K4RACTU package="0603 [SMD, multilayer]"]
  C54 = Ceramic Capacitor [capacitance=1µF part_number=C0603C105K4RACTU package="0603 [SMD, multilayer]"]
  C55 = Ceramic Capacitor [capacitance=0.01µF part_number=C0603C103K4RACTU package="0603 [SMD, multilayer]"]
  R39 = Resistor [tolerance=±5% resistance=100 part_number=RC0603FR-07100RL package="0603 [SMD]"]
  R40 = Resistor [tolerance=±5% resistance=100 part_number=RC0603FR-07100RL package="0603 [SMD]"]
  R41 = Resistor [tolerance=±5% resistance=1M part_number=RC0603FR-071ML package="0603 [SMD]"]
  J24 = Screw terminal - 2 pins [package=THT]
  C56 = Ceramic Capacitor [capacitance=0.1µF part_number=C0603C104K4RACTU package="0603 [SMD, multilayer]"]
  C57 = Tantalum Capacitor [capacitance=10µF part_number=C0603C104K4RACTU package="A 3216 [SMD, tantalum]"]
  U9 = AD8495 SMD [package=msop8]
  C58 = Ceramic Capacitor [capacitance=0.01µF part_number=C0603C103K4RACTU package="0603 [SMD, multilayer]"]
  C59 = Ceramic Capacitor [capacitance=1µF part_number=C0603C105K4RACTU package="0603 [SMD, multilayer]"]
  C60 = Ceramic Capacitor [capacitance=0.01µF part_number=C0603C103K4RACTU package="0603 [SMD, multilayer]"]
  R42 = Resistor [tolerance=±5% resistance=100 part_number=RC0603FR-07100RL package="0603 [SMD]"]
  R43 = Resistor [tolerance=±5% resistance=100 part_number=RC0603FR-07100RL package="0603 [SMD]"]
  R44 = Resistor [tolerance=±5% resistance=1M part_number=RC0603FR-071ML package="0603 [SMD]"]
  J25 = Screw terminal - 2 pins [package=THT]
  C61 = Ceramic Capacitor [capacitance=0.1µF part_number=C0603C104K4RACTU package="0603 [SMD, multilayer]"]
  C62 = Tantalum Capacitor [capacitance=10µF part_number=C0603C104K4RACTU package="A 3216 [SMD, tantalum]"]
  U10 = AD8495 SMD [package=msop8]
  C63 = Ceramic Capacitor [capacitance=0.01µF part_number=C0603C103K4RACTU package="0603 [SMD, multilayer]"]
  C64 = Ceramic Capacitor [capacitance=1µF part_number=C0603C105K4RACTU package="0603 [SMD, multilayer]"]
  C65 = Ceramic Capacitor [capacitance=0.01µF part_number=C0603C103K4RACTU package="0603 [SMD, multilayer]"]
  R45 = Resistor [tolerance=±5% resistance=100 part_number=RC0603FR-07100RL package="0603 [SMD]"]
  R46 = Resistor [tolerance=±5% resistance=100 part_number=RC0603FR-07100RL package="0603 [SMD]"]
  R47 = Resistor [tolerance=±5% resistance=1M part_number=RC0603FR-071ML package="0603 [SMD]"]
  J26 = Screw terminal - 2 pins [package=THT]
  C66 = Ceramic Capacitor [capacitance=0.1µF part_number=C0603C104K4RACTU package="0603 [SMD, multilayer]"]
  C67 = Tantalum Capacitor [capacitance=10µF part_number=C0603C104K4RACTU package="A 3216 [SMD, tantalum]"]
  Part1 = Arduino Mega 2560 (Rev3)

nets:
  ssr1: J13.pin1, Part1.D22
  GND: J13.pin2, J13.pin4, J13.pin6, J13.pin8, J1.pin2, U5.pin2, J18.pin3, J19.pin3, J20.pin3, J21.pin3, J22.pin3, C45.-, C46.-, C47.0, C17.1, C23.0, C26.0, C29.-, R35.Pin_0, J2.pin1, U6.REF, U6.-VS, U7.REF, U7.-VS, C48.1, C50.0, R38.Pin_0, C51.0, C52.-, U8.REF, U8.-VS, C53.1, C55.0, R41.Pin_0, C56.0, C57.-, U9.REF, U9.-VS, C58.1, C60.0, R44.Pin_0, C61.0, C62.-, U10.REF, U10.-VS, C63.1, C65.0, R47.Pin_0, C66.0, C67.-, Part1.GND
  ssr2: J13.pin3, Part1.D24
  ssr3: J13.pin5, Part1.D26
  ssr4: J13.pin7, Part1.D28
  5V: J1.pin1, J18.pin2, J19.pin2, J20.pin2, J21.pin2, J22.pin2, C46.+, C26.1, C29.+, U6.VS+, U7.VS+, C51.1, C52.+, U8.VS+, C56.1, C57.+, U9.VS+, C61.1, C62.+, U10.VS+, C66.1, C67.+, Part1.VIN
  sda: J1.pin3, Part1.D20/SDA
  slc: J1.pin4, Part1.D21/SCL
  enc 1: J1.pin5, Part1.D17_PWM/RX2
  enc 2: J1.pin6, Part1.D18/TX1
  button: J1.pin7, Part1.D19/RX1
  RO: J14.pin1, Part1.D7_PWM
  RE: J14.pin2, Part1.D6_PWM
  DE: J14.pin3, Part1.D5_PWM
  DI: J14.pin4, Part1.D4_PWM
  N1: J11.pin1, R32.Pin_0, R35.Pin_1
  N2: J11.pin2, R29.Pin_0
  N3: U5.pin1, C45.+, J2.pin2
  N4: U5.pin3, C47.1
  pwm sig: J18.pin1, Part1.D9_PWM
  aux 1: J19.pin1, Part1.D11_PWM
  aux 2: J20.pin1, Part1.D12_PWM
  aux 3: J21.pin1, Part1.D13_PWM
  aux: J22.pin1, Part1.D10_PWM
  N5: C17.0, C20.1, U6.+IN, R29.Pin_1
  N6: C23.1, C20.0, R32.Pin_1, U6.-IN
  TC1: U6.SENSE, U6.OUT, Part1.A0
  N7: U7.-IN, C49.0, C50.1, R37.Pin_1
  TC2: U7.SENSE, U7.OUT, Part1.A1
  N8: U7.+IN, C48.0, C49.1, R36.Pin_1
  N9: R36.Pin_0, J23.pin2
  N10: R37.Pin_0, R38.Pin_1, J23.pin1
  N11: U8.-IN, C54.0, C55.1, R40.Pin_1
  TC3: U8.SENSE, U8.OUT, Part1.A2
  N12: U8.+IN, C53.0, C54.1, R39.Pin_1
  N13: R39.Pin_0, J24.pin2
  N14: R40.Pin_0, R41.Pin_1, J24.pin1
  N15: U9.-IN, C59.0, C60.1, R43.Pin_1
  TC4: U9.SENSE, U9.OUT, Part1.A3
  N16: U9.+IN, C58.0, C59.1, R42.Pin_1
  N17: R42.Pin_0, J25.pin2
  N18: R43.Pin_0, R44.Pin_1, J25.pin1
  N19: U10.-IN, C64.0, C65.1, R46.Pin_1
  TC5: U10.SENSE, U10.OUT, Part1.A4
  N20: U10.+IN, C63.0, C64.1, R45.Pin_1
  N21: R45.Pin_0, J26.pin2
  N22: R46.Pin_0, R47.Pin_1, J26.pin1

notes:
  power in
  control pannel
  Relay Out
  thermocouple 1
  VFD Breakout
  Pwm controller
  Open Extruder
  Control Board
  V1.1
  thermocouple 2
  thermocouple 3
  thermocouple 4
  thermocouple 5

custom parts:
  AD8495 SMD: AD8495 SMD Chip
