# Fritzing sketch extruder control (saved by Fritzing 0.9.3b)
breadboards: 1

parts:
  Part1 = Arduino Mega 2560 (Rev3)
  R1 = Resistor [tolerance=±5% resistance=10 package=THT]
  R2 = Resistor [tolerance=±5% resistance=100k package=THT]
  Q1 = Basic FET P-Channel [package="TO220 [THT]"]
  J1 = Screw terminal - 2 pins [package=THT]
  R4 = Resistor [tolerance=±5% resistance=10 package=THT]
  R5 = Resistor [tolerance=±5% resistance=100k package=THT]
  Q2 = Basic FET P-Channel [package="TO220 [THT]"]
  J2 = Screw terminal - 2 pins [package=THT]
  R7 = Resistor [tolerance=±5% resistance=10 package=THT]
  R8 = Resistor [tolerance=±5% resistance=10 package=THT]
  R10 = Resistor [tolerance=±5% resistance=100k package=THT]
  Q3 = Basic FET P-Channel [package="TO220 [THT]"]
  Q4 = Basic FET P-Channel [package="TO220 [THT]"]
  J3 = Screw terminal - 2 pins [package=THT]
  J4 = Screw terminal - 2 pins [package=THT]
  R13 = Resistor [tolerance=±5% resistance=10 package=THT]
  R14 = Resistor [tolerance=±5% resistance=10 package=THT]
  R15 = Resistor [tolerance=±5% resistance=100k package=THT]
  R16 = Resistor [tolerance=±5% resistance=100k package=THT]
  Q5 = Basic FET P-Channel [package="TO220 [THT]"]
  Q6 = Basic FET P-Channel [package="TO220 [THT]"]
  J5 = Screw terminal - 2 pins [package=THT]
  J6 = Screw terminal - 2 pins [package=THT]
  C2 = Ceramic Capacitor [capacitance=1µF package="100 mil [THT, multilayer]"]
  C3 = Ceramic Capacitor [capacitance=0.01µF package="100 mil [THT, multilayer]"]
  IC1 = SO08 [chip_label=AD8495 package=SO]
  J7 = Screw terminal - 2 pins [package=THT]
  C6 = Ceramic Capacitor [capacitance=0.01µF package="100 mil [THT, multilayer]"]
  C7 = Ceramic Capacitor [capacitance=1µF package="100 mil [THT, multilayer]"]
  R24 = Resistor [tolerance=±5% resistance=1M package=THT]
  IC2 = SO08 [chip_label=AD8495 package=SO]
  J8 = Screw terminal - 2 pins [package=THT]
  C11 = Ceramic Capacitor [capacitance=0.01µF package="100 mil [THT, multilayer]"]
  C12 = Ceramic Capacitor [capacitance=1µF package="100 mil [THT, multilayer]"]
  C13 = Ceramic Capacitor [capacitance=0.01µF package="100 mil [THT, multilayer]"]
  R26 = Resistor [tolerance=±5% resistance=100 package=THT]
  R27 = Resistor [tolerance=±5% resistance=1M package=THT]
  IC3 = SO08 [chip_label=AD8495 package=SO]
  J9 = Screw terminal - 2 pins [package=THT]
  J10 = Screw terminal - 2 pins [package=THT]
  F1 = FUSE [package=fuse_5mm]
  U1 = mystery part, 3 pins [chip_label=LM7805]
  U2 = mystery part, 3 pins [chip_label=LM7812]
  J11 = Camdenboss CTB0158-4 [part_number=CTB0158-4 package=THT]
  J12 = Camdenboss CTB0158-4 [part_number=CTB0158-4 package=THT]
  J13 = Camdenboss CTB0158-4 [part_number=CTB0158-4 package=THT]
  ENCODER1 = Rotary Encoder with switch (KY-040) [part_number=KY-040]
  C10 = Tantalum Capacitor [capacitance=10µF package="B 3528 [SMD, tantalum]"]
  C5 = Tantalum Capacitor [capacitance=10µF package="B 3528 [SMD, tantalum]"]
  C19 = Tantalum Capacitor [capacitance=47µF package="B 3528 [SMD, tantalum]"]
  C16 = Tantalum Capacitor [capacitance=47µF package="B 3528 [SMD, tantalum]"]
  C26 = Tantalum Capacitor [capacitance=10µF package="B 3528 [SMD, tantalum]"]
  C20 = Tantalum Capacitor [capacitance=10µF package="B 3528 [SMD, tantalum]"]
  C22 = Tantalum Capacitor [capacitance=47µF package="B 3528 [SMD, tantalum]"]
  C15 = Tantalum Capacitor [capacitance=10µF voltage=6.3V package="B 3528 [SMD, tantalum]"]
  R20 = Resistor [tolerance=±5% resistance=100 package="0805 [SMD]"]
  R25 = Resistor [tolerance=±5% resistance=100 package="0805 [SMD]"]
  R23 = Resistor [tolerance=±5% resistance=100 package="0805 [SMD]"]
  R22 = Resistor [tolerance=±5% resistance=100 package="0805 [SMD]"]
  C25 = Ceramic Capacitor [capacitance=1µF package="0805 [SMD, multilayer]"]
  LED6 = smd LED [color="Red (633nm)" package="0805 [SMD]"]
  LED5 = smd LED [color="Red (633nm)" package="0805 [SMD]"]
  LED4 = smd LED [color="Red (633nm)" package="0805 [SMD]"]
  LED2 = smd LED [color="Red (633nm)" package="0805 [SMD]"]
  LED3 = smd LED [color="Red (633nm)" package="0805 [SMD]"]
  LED1 = smd LED [color="Red (633nm)" package="0805 [SMD]"]
  C1 = Ceramic Capacitor [capacitance=0.01µF package="0805 [SMD, multilayer]"]
  C9 = Ceramic Capacitor [capacitance=0.1µF package="0805 [SMD, multilayer]"]
  C18 = Ceramic Capacitor [capacitance=0.1µF package="0805 [SMD, multilayer]"]
  C24 = Ceramic Capacitor [capacitance=0.1µF package="0805 [SMD, multilayer]"]
  C21 = Ceramic Capacitor [capacitance=0.1µF package="0805 [SMD, multilayer]"]
  C14 = Ceramic Capacitor [capacitance=0.1µF package="0805 [SMD, multilayer]"]
  C4 = Ceramic Capacitor [capacitance=0.1µF package="0805 [SMD, multilayer]"]
  C8 = Ceramic Capacitor [capacitance=0.01µF package="0805 [SMD, multilayer]"]
  R17 = Resistor [tolerance=±5% resistance=1.8k package="0805 [SMD]"]
  R12 = Resistor [tolerance=±5% resistance=1.8k package="0805 [SMD]"]
  R18 = Resistor [tolerance=±5% resistance=1.8k package="0805 [SMD]"]
  R3 = Resistor [tolerance=±5% resistance=1.8k package="0805 [SMD]"]
  R6 = Resistor [tolerance=±5% resistance=1.8k package="0805 [SMD]"]
  R11 = Resistor [tolerance=±5% resistance=1.8k package="0805 [SMD]"]
  R19 = Resistor [tolerance=±5% resistance=100 package="0805 [SMD]"]
  R21 = Resistor [tolerance=±5% resistance=1M package="0805 [SMD]"]
  R9 = Resistor [tolerance=±5% resistance=100k package="0805 [SMD]"]

nets:
  TC1: Part1.A1, IC1.5, IC1.6
  TC2: Part1.A2, IC2.5, IC2.6
  TC3: Part1.A3, IC3.5, IC3.6
  SCL: Part1.D21/SCL, Part1.SCL, J13.pin1
  SDA: Part1.D20/SDA, Part1.SDA, J13.pin2
  heater 1_1: Part1.D8_PWM, R1.Pin_0, R2.Pin_0
  5V/GND: Part1.GND, R2.Pin_1, Q1.source, R5.Pin_1, Q2.source, R10.Pin_1, Q3.source, Q4.source, R15.Pin_1, R16.Pin_1, Q5.source, Q6.source, C3.0, IC1.7, C6.1, IC2.7, C11.1, C13.0, IC3.7, J10.pin1, U1.pin2, U2.pin2, J11.pin4, J12.pin4, J13.pin3, J13.pin4, ENCODER1.GND, ENCODER1.+, C10.+, C5.+, C19.-, C16.-, C26.-, C26.+, C20.-, C22.-, C15.+, C25.0, C1.1, C9.1, C18.0, C24.0, C21.0, C14.1, C4.1, C8.0, R9.Pin_1
  12V: Part1.VIN, U2.pin3, C20.+, C21.1
  heater 3_2: Part1.D2_PWM, R13.Pin_0, R15.Pin_0
  heater 3_1: Part1.D4_PWM, R14.Pin_0, R16.Pin_0
  heater 2_2: Part1.D5_PWM, R8.Pin_0, R10.Pin_0
  heater 2_1: Part1.D6_PWM, R7.Pin_0, R9.Pin_0
  heater 1_2: Part1.D7_PWM, R4.Pin_0, R5.Pin_0
  STEP_1: Part1.D38, J11.pin1
  DIR_1: Part1.D39, J11.pin2
  ENA_1: Part1.D40, J11.pin3
  STEP_2: Part1.D41, J12.pin1
  DIR_2: Part1.D42, J12.pin2
  ENA_2: Part1.D43, J12.pin3
  CLK: Part1.D44, ENCODER1.CLK
  DT: Part1.D45, ENCODER1.DT
  SW: Part1.D46, ENCODER1.SW
  N1: R1.Pin_1, Q1.gate
  N2: Q1.drain, J1.pin1, LED1.cathode
  24V: J1.pin2, J2.pin2, J3.pin2, J4.pin2, J5.pin2, J6.pin2, F1.2, U1.pin1, C16.+, C22.+, C25.1, C24.1, R17.Pin_1, R12.Pin_1, R18.Pin_1, R3.Pin_1, R6.Pin_1, R11.Pin_1
  N3: R4.Pin_1, Q2.gate
  N4: Q2.drain, J2.pin1, LED2.cathode
  N5: R7.Pin_1, Q3.gate
  N6: R8.Pin_1, Q4.gate
  N7: Q3.drain, J3.pin1, LED4.cathode
  N8: Q4.drain, J4.pin1, LED3.cathode
  N9: R13.Pin_1, Q6.gate
  N10: R14.Pin_1, Q5.gate
  N11: Q5.drain, J6.pin1, LED5.cathode
  N12: Q6.drain, J5.pin1, LED6.cathode
  N13: C2.0, C3.1, IC1.1, R20.Pin_0
  N14: C2.1, IC1.8, C1.0, R19.Pin_0
  N15: IC1.2, IC1.3, C5.-, C4.0, R21.Pin_0
  N16: J7.pin1, R19.Pin_1
  N17: J7.pin2, R20.Pin_1, R21.Pin_1
  N18: C6.0, C7.1, IC2.8, R22.Pin_0
  N19: C7.0, IC2.1, R23.Pin_0, C8.1
  N20: R24.Pin_0, IC2.2, IC2.3, C10.-, C9.0
  N21: R24.Pin_1, J8.pin2, R23.Pin_1
  N22: J8.pin1, R22.Pin_1
  N23: C11.0, C12.1, IC3.8, R25.Pin_0
  N24: C12.0, C13.1, R26.Pin_0, IC3.1
  N25: R26.Pin_1, R27.Pin_1, J9.pin2
  N26: R27.Pin_0, IC3.2, IC3.3, C15.-, C14.0
  N27: J9.pin1, R25.Pin_1
  N28: J10.pin2, F1.1
  N29: U1.pin3, C18.1
  N30: U2.pin1, C19.+
  N31: LED6.anode, R17.Pin_0
  N32: LED5.anode, R18.Pin_0
  N33: LED4.anode, R11.Pin_0
  N34: LED2.anode, R6.Pin_0
  N35: LED3.anode, R12.Pin_0
  N36: LED1.anode, R3.Pin_0

custom parts:
  Rotary Encoder with switch (KY-040): A Rotary Encoder with switch
